// Logisim project 16 bit computer.circ as structural Verilog
module CPU (
  input  in_1,
  output [7:0] out_2,
  output [7:0] out_3,
  output [7:0] out_4,
  output [7:0] out_5,
  output [7:0] out_6,
  output [7:0] out_7,
  output [7:0] out_8,
  output [7:0] out_9,
  output [7:0] out_10,
  output [7:0] out_11,
  output [7:0] out_12,
  output [7:0] out_13
);

  wire and_1_out, and_2_out, and_3_out, and_4_out, and_5_out, and_6_out, clock_1_out;
  wire [7:0] ram_1_data;
  wire [15:0] counter_1_q;

  Counter #(.width(16), .max('hffff), .trigger("falling")) counter_1 (
    .count(in_1), .Q(counter_1_q), .clk(clock_1_out));  // open: load, D, carry, clr
  Clock clock_1 (.out(clock_1_out));
  RAM #(.addrWidth(16)) ram_1 (.addr(counter_1_q), .data(ram_1_data), .clk(clock_1_out));  // open: sel, ld, clr
  and and_1 (and_1_out, ram_1_data[0], ~ram_1_data[1], ~ram_1_data[2], ~ram_1_data[3], ~ram_1_data[4], ~ram_1_data[5], ~ram_1_data[6], ~ram_1_data[7]);  // AND_Gate
  and and_2 (and_2_out, ~ram_1_data[0], ram_1_data[1], ~ram_1_data[2], ~ram_1_data[3], ~ram_1_data[4], ~ram_1_data[5], ~ram_1_data[6], ~ram_1_data[7]);  // AND_Gate
  and and_3 (and_3_out, ram_1_data[0], ram_1_data[1], ~ram_1_data[2], ~ram_1_data[3], ~ram_1_data[4], ~ram_1_data[5], ~ram_1_data[6], ~ram_1_data[7]);  // AND_Gate
  and and_4 (and_4_out, ~ram_1_data[0], ~ram_1_data[1], ram_1_data[2], ~ram_1_data[3], ~ram_1_data[4], ~ram_1_data[5], ~ram_1_data[6], ~ram_1_data[7]);  // AND_Gate
  and and_5 (and_5_out, ram_1_data[0], ~ram_1_data[1], ram_1_data[2], ~ram_1_data[3], ~ram_1_data[4], ~ram_1_data[5], ~ram_1_data[6], ~ram_1_data[7]);  // AND_Gate
  and and_6 (and_6_out, ~ram_1_data[0], ram_1_data[1], ram_1_data[2], ~ram_1_data[3], ~ram_1_data[4], ~ram_1_data[5], ~ram_1_data[6], ~ram_1_data[7]);  // AND_Gate
  _16_Bit_Register ax (
    .mov_ax_value16(and_1_out), .Data(ram_1_data), .CLK(clock_1_out), .ah(out_2), .al(out_3));  // open: mov_ah_value8, mov_al_value8
  _16_Bit_Register bx (
    .mov_ax_value16(and_2_out), .Data(ram_1_data), .CLK(clock_1_out), .ah(out_4), .al(out_5));  // open: mov_ah_value8, mov_al_value8
  _16_Bit_Register cx (
    .mov_ax_value16(and_3_out), .Data(ram_1_data), .CLK(clock_1_out), .ah(out_6), .al(out_7));  // open: mov_ah_value8, mov_al_value8
  _16_Bit_Register dx (
    .mov_ax_value16(and_4_out), .Data(ram_1_data), .CLK(clock_1_out), .ah(out_8), .al(out_9));  // open: mov_ah_value8, mov_al_value8
  _16_Bit_Register sp (
    .mov_ax_value16(and_5_out), .Data(ram_1_data), .CLK(clock_1_out), .ah(out_10), .al(out_11));  // open: mov_ah_value8, mov_al_value8
  _16_Bit_Register ip (
    .mov_ax_value16(and_6_out), .Data(ram_1_data), .CLK(clock_1_out), .ah(out_12), .al(out_13));  // open: mov_ah_value8, mov_al_value8
endmodule

module Register_small (
  input  mov_ah_value8,
  input  mov_al_value8,
  input  [7:0] Data_In,
  input  CLK,
  output [7:0] ah,
  output [7:0] al
);

  wire [7:0] transistor_1_out, transistor_2_out;

  Transistor #(.\type ("n"), .width(8)) transistor_1 (.in(Data_In), .out(transistor_1_out), .gate(mov_ah_value8));
  Transistor #(.\type ("n"), .width(8)) transistor_2 (.in(Data_In), .out(transistor_2_out), .gate(mov_al_value8));
  Register u_ah (.D(transistor_1_out), .en(mov_ah_value8), .Q(ah), .clk(CLK));  // open: clr
  Register u_al (.D(transistor_2_out), .en(mov_al_value8), .Q(al), .clk(CLK));  // open: clr
endmodule

module _2_cycle (
  input  Active,
  input  CLK,
  output Trigger
);

  wire and_1_out, d_ff_1_qn, or_1_out, t_ff_1_q;

  D_Flip_Flop d_ff_1 (
    .clk(CLK), .D(and_1_out), .Q(Trigger), .Qn(d_ff_1_qn), .en(or_1_out), .reset(t_ff_1_q));  // open: preset
  and and_1 (and_1_out, ~Trigger, Active);  // AND_Gate
  or or_1 (or_1_out, and_1_out, t_ff_1_q);
  T_Flip_Flop t_ff_1 (.clk(CLK), .T(Trigger), .Q(t_ff_1_q), .reset(d_ff_1_qn), .en(CLK));  // open: Qn, preset
endmodule

module _3_cycle (
  input  Active,
  input  CLK,
  output _1,
  output _2,
  output _3
);

  wire and_1_out, and_2_out, and_3_out, or_1_out;

  and and_1 (and_1_out, ~or_1_out, Active);  // AND_Gate
  D_Flip_Flop d_ff_1 (.clk(CLK), .D(and_2_out), .Q(_1));  // open: Qn, preset, en, reset
  and and_2 (and_2_out, ~_1, and_1_out);  // AND_Gate
  T_Flip_Flop t_ff_1 (.clk(CLK), .T(_1), .Q(_2), .reset(and_3_out), .en(CLK));  // open: Qn, preset
  and and_3 (and_3_out, _2, _3);
  or or_1 (or_1_out, _1, _2);
  D_Flip_Flop d_ff_2 (.clk(CLK), .D(_2), .Q(_3));  // open: Qn, preset, en, reset
endmodule

module _16_Bit_Register (
  input  mov_ax_value16,
  input  mov_ah_value8,
  input  mov_al_value8,
  input  [7:0] Data,
  input  CLK,
  output [7:0] ah,
  output [7:0] al
);

  wire n2_cycle_1_trigger, n2_cycle_2_trigger, n3_cycle_1__1, or_1_out, or_2_out, or_3_out;
  wire [7:0] transistor_1_out;

  or or_1 (or_1_out, mov_ax_value16, mov_ah_value8);
  or or_2 (or_2_out, n3_cycle_1__1, mov_al_value8);
  _3_cycle u_3_cycle_1 (.Active(mov_ax_value16), .CLK(CLK), ._1(n3_cycle_1__1));  // open: _2, _3
  _2_cycle u_2_cycle_1 (.Active(or_1_out), .CLK(CLK), .Trigger(n2_cycle_1_trigger));
  _2_cycle u_2_cycle_2 (.Active(or_2_out), .CLK(CLK), .Trigger(n2_cycle_2_trigger));
  or or_3 (or_3_out, n2_cycle_1_trigger, n2_cycle_2_trigger);
  Transistor #(.\type ("n"), .width(8)) transistor_1 (.in(Data), .out(transistor_1_out), .gate(or_3_out));
  Register_small ax (
    .mov_ah_value8(n2_cycle_1_trigger), .mov_al_value8(n2_cycle_2_trigger), .Data_In(transistor_1_out),
    .CLK(CLK), .ah(ah), .al(al));
endmodule

module ip_Register (
  input  mov_ip_value16,
  input  mov_iph_value8,
  input  mov_ipl_value8,
  input  [7:0] Data,
  input  CLK,
  output [7:0] ah,
  output [7:0] al
);

  wire n2_cycle_1_trigger, n2_cycle_2_trigger, n3_cycle_1__1, or_1_out, or_2_out, or_3_out;
  wire [7:0] transistor_1_out;

  or or_1 (or_1_out, mov_ip_value16, mov_iph_value8);
  or or_2 (or_2_out, n3_cycle_1__1, mov_ipl_value8);
  _3_cycle u_3_cycle_1 (.Active(mov_ip_value16), .CLK(CLK), ._1(n3_cycle_1__1));  // open: _2, _3
  _2_cycle u_2_cycle_1 (.Active(or_1_out), .CLK(CLK), .Trigger(n2_cycle_1_trigger));
  _2_cycle u_2_cycle_2 (.Active(or_2_out), .CLK(CLK), .Trigger(n2_cycle_2_trigger));
  or or_3 (or_3_out, n2_cycle_1_trigger, n2_cycle_2_trigger);
  Transistor #(.\type ("n"), .width(8)) transistor_1 (.in(Data), .out(transistor_1_out), .gate(or_3_out));
  Register_small ax (
    .mov_ah_value8(n2_cycle_1_trigger), .mov_al_value8(n2_cycle_2_trigger), .Data_In(transistor_1_out),
    .CLK(CLK), .ah(ah), .al(al));
endmodule

module ip_Register_small (
  input  mov_ip_value16,
  input  [15:0] in_2,
  input  CLK,
  input  mov_iph_value8,
  input  mov_ipl_value8,
  input  [7:0] Data_In,
  input  CLK_2,
  output [7:0] iph,
  output [7:0] ipl
);

  wire and_1_out, counter_2_carry, not_1_out;
  wire [7:0] transistor_1_out, transistor_2_out;
  wire [15:0] counter_1_q;

  not not_1 (not_1_out, mov_ip_value16);
  and and_1 (and_1_out, ~mov_iph_value8, ~mov_ipl_value8);  // AND_Gate
  Counter #(.width(16), .max('hffff)) counter_1 (
    .load(mov_ip_value16), .D(in_2), .count(not_1_out), .Q(counter_1_q), .clk(CLK));  // open: carry, clr
  Transistor #(.\type ("n"), .width(8)) transistor_1 (.in(Data_In), .out(transistor_1_out), .gate(mov_iph_value8));
  Transistor #(.\type ("n"), .width(8)) transistor_2 (.in(Data_In), .out(transistor_2_out), .gate(mov_ipl_value8));
  Counter #(.trigger("falling")) counter_2 (
    .load(mov_iph_value8), .D(transistor_1_out), .count(and_1_out), .Q(iph), .carry(counter_2_carry),
    .clk(CLK_2));  // open: clr
  Counter #(.trigger("falling")) counter_3 (
    .load(mov_ipl_value8), .D(transistor_2_out), .count(counter_2_carry), .Q(ipl), .clk(CLK_2));  // open: carry, clr
endmodule
